# Fritzing sketch projet SmartPatate1 (saved by Fritzing 0.9.3b)
breadboards: 1

parts:
  Composant1 = Arduino Uno (Rev3)
  R6 = Resistor [tolerance=±5% resistance=470 package=THT]
  LED3 = LED - 5mm [color="Red (633nm)" package="5 mm [THT]"]
  LED1 = LED - 5mm [color="Yellow (595nm)" package="5 mm [THT]"]
  LED2 = LED - 5mm [color="Green (555nm)" package="5 mm [THT]"]
  C2 = Ceramic Capacitor [capacitance=0.1nF package="100 mil [THT, multilayer]"]
  R1 = Resistor [tolerance=±5% resistance=10k package=THT]
  D1 = Rectifier Diode [part_number=1N4001 package="300 mil [THT]"]
  C1 = Ceramic Capacitor [capacitance=10nF package="100 mil [THT, multilayer]"]
  R2 = Resistor [tolerance=±5% resistance=3.3k package=THT]
  L1 = Inductor [package="400 mil [THT]"]
  R4 = Resistor [tolerance=±5% resistance=470 package=THT]
  R5 = Resistor [tolerance=±5% resistance=470 package=THT]
  R3 = Resistor [tolerance=±5% resistance=1M package=THT]

nets:
  N1: Composant1.A0, C2.0, D1.cathode, R3.Pin_1
  N2: Composant1.D9_PWM, R6.Pin_0, R1.Pin_1, R4.Pin_0, R5.Pin_0
  GND: Composant1.GND, C2.1, R2.Pin_0, R3.Pin_0
  N3: Composant1.D2, LED3.anode
  N4: Composant1.D4, LED2.anode
  N5: Composant1.D7, LED1.anode
  N6: R6.Pin_1, LED3.cathode
  N7: LED1.cathode, R4.Pin_1
  N8: LED2.cathode, R5.Pin_1
  N9: R1.Pin_0, R2.Pin_1, L1.pin_1
  N10: D1.anode, C1.0, L1.pin_0
  Patate: C1.1
